# Fritzing sketch scetch (saved by Fritzing 0.9.3b)
breadboards: 1

parts:
  WeMos_D1_Mini1 = WeMos D1 Mini
  TD-er1 = MH-Z19 CO2 sensor [part_number=MH-Z19]

nets:
  5V: WeMos_D1_Mini1.5V, TD-er1.Vin
  N1: WeMos_D1_Mini1.D0, WeMos_D1_Mini1.RST
  N2: WeMos_D1_Mini1.D1, WeMos_D1_Mini1.D2, TD-er1.Vout, TD-er1.RX, TD-er1.TX
  N3: WeMos_D1_Mini1.G, TD-er1.GND
